// Logisim project binario-gray.circ as structural Verilog: 1 circuit, main circuit main
module main (
  input  B3,
  input  B2,
  input  in_3,
  input  B0,
  output G3,
  output G2,
  output G1,
  output G0
);

  xor xor_1 (G2, B3, B2);
  xor xor_2 (G1, B2, in_3);
  xor xor_3 (G0, in_3, B0);

  assign G3 = B3;

  // Notes on the sheet:
  //   B1
endmodule
